# Fritzing sketch LED_sch (saved by Fritzing 0.9.6b)

parts:
  Componente1 = Arduino Uno (Rev3)
  R1 = Resistor [tolerance=±5% resistance=220 package="2512 [SMD]"]
  LED2 = smd LED [color="Red (633nm)" package="1206 [SMD]"]

nets:
  N1: Componente1.D8, R1.Pin_1
  N2: Componente1.GND, LED2.cathode
  N3: R1.Pin_0, LED2.anode
