# Fritzing sketch Pulsador_sch (saved by Fritzing 0.9.6b)
breadboards: 1

parts:
  Componente1 = Arduino Uno (Rev3) - ICSP
  S1 = Momentary Switch [package=ksa_sealed_tac_switch]
  S2 = Momentary Switch [package=ksa_sealed_tac_switch]
  R1 = Resistor [tolerance=±5% resistance=10k package="0603 [SMD]"]

nets:
  N1: Componente1.GND, S2.3, R1.Pin_0
  N2: Componente1.D2, S2.2
  N3: Componente1.D3_PWM, S1.2
  N4: Componente1.5V, S1.4
  N5: S1.1, R1.Pin_1

notes:
  Resistencia Pull-Up interna.
  Resistencia Pull-Down externa.
