# Fritzing sketch TrackingMultiple_sch (saved by Fritzing 0.9.6b)

parts:
  A1 = 3channel line follower module
  Componente1 = Arduino Uno (Rev3) - ICSP

nets:
  N1: A1.Pin_1, Componente1.D5_PWM
  N2: A1.Pin_2, Componente1.D6_PWM
  N3: A1.Pin_3, Componente1.D7
  N4: A1.Pin_4, Componente1.GND
  N5: A1.Pin_5, Componente1.5V

custom parts:
  3channel line follower module: 3 channel line follower module.
