# Fritzing sketch TrackingSimple_sch (saved by Fritzing 0.9.6b)

parts:
  Componente1 = Arduino Uno (Rev3) - ICSP
  M1 = fc-51 [package=THT]

nets:
  N1: Componente1.D4, M1.pin1
  N2: Componente1.5V, M1.pin3
  N3: Componente1.GND, M1.pin2
