# Fritzing sketch Ultrasonic_sch (saved by Fritzing 0.9.6b)

parts:
  Componente1 = Arduino Uno (Rev3) - ICSP
  HC-SR04_Sensor_1 = HC-SR04 Ultrasonic Distance Sensor

nets:
  N1: Componente1.D2, HC-SR04_Sensor_1.TRIG
  N2: Componente1.D3_PWM, HC-SR04_Sensor_1.ECHO
  5V: Componente1.5V, HC-SR04_Sensor_1.VCC
  GND: Componente1.GND, HC-SR04_Sensor_1.GND
